// Logisim project Exemplo.circ as structural Verilog: 1 circuit, main circuit Exemplo
module Exemplo (
  input  A,
  input  B,
  input  C,
  output Y
);

  wire and_1_out, not_1_out;

  and and_1 (and_1_out, A, B);
  not not_1 (not_1_out, C);
  or or_1 (Y, and_1_out, not_1_out);
endmodule
